# Fritzing sketch Brausteuerung RasPi 3 (saved by Fritzing 0.9.6b)
breadboards: 1

parts:
  Raspberry_Pi_1 = Raspberry Pi 3 [part_number=RPI-3-V1.2]
  KY-1 = Keyes Relay [package=THT]
  KY-2 = Keyes Relay [package=THT]
  J1 = Piezo Speaker
  Bauteil1 = Adafruit MAX31856 Thermocouple Amp [part_number="Adafruit #3263"]
  SW1 = ENCODER_RGB_CA [package=encoder_led_3]
  Q1 = PNP-Transistor [package="TO92 [THT]"]
  R1 = Resistor [tolerance=±5% resistance=220 package="2010 [SMD]"]
  Grove1 = Grove OLED 128x96

nets:
  3V3: Raspberry_Pi_1.3v3, Raspberry_Pi_1.3V3, Bauteil1.3.3V, SW1.+, Grove1.VCC
  N1: Raspberry_Pi_1.GPIO2, Grove1.SDA
  N2: Raspberry_Pi_1.GPIO3, Grove1.SCL
  N3: Raspberry_Pi_1.GIPO17, KY-2.sSgnal
  N4: Raspberry_Pi_1.GIPO10, Bauteil1.SDI
  N5: Raspberry_Pi_1.GIPO9, Bauteil1.SDO
  N6: Raspberry_Pi_1.GIPO11, Bauteil1.SCK
  GND: Raspberry_Pi_1.GND, KY-1.ground, Bauteil1.GND, SW1.-B, Q1.C, Grove1.GND
  N7: Raspberry_Pi_1.GIPO25, SW1.SW
  N8: Raspberry_Pi_1.GIPO24, R1.Pin_0
  N9: Raspberry_Pi_1.GIPO23, Bauteil1.!CS
  N10: Raspberry_Pi_1.GIPO18, KY-1.sSgnal
  N11: Raspberry_Pi_1.GIPO15, SW1.-G
  N12: Raspberry_Pi_1.GIPO14, SW1.-R
  N13: Raspberry_Pi_1.5V, KY-1.power, KY-2.power, J1.pin2
  N14: J1.pin1, Q1.E
  N15: Q1.B, R1.Pin_1

notes:
  5V
  Rote Steck-dose
  Blaue Steck-dose
  3.3V
  PT100 Temperatur-Sensor

custom parts:
  Keyes Relay: The Keyes 5V relay module is suitable for SCM development, home appliance control. It uses a 5V~12V TIL control signal which can control DC / AC signal.
  Adafruit MAX31856 Thermocouple Amp: Thermocouples are very sensitive, requiring a good amplifier with a cold-compensation reference, as well as calculations to handle any non-linearities. For a long time we've suggested our MAX31855K breakout, which works great but is only for K-type thermocouples. Now we're happy to offer a great new thermocouple amplifier/converter that can handle just about any type of thermocouple, and even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
